# Fritzing sketch breadboard (saved by Fritzing 0.9.3b)
breadboards: 4

parts:
  Microcontroller = IC, DIP package, 40 pins [chip_label="Atmega 162"]
  RESET = Pushbutton [package="[SMD]"]
  LED = LED - 3mm [color="Red (633nm)" package="3 mm [THT]"]
  VCC1 = Battery block 9V
  C3 = Capacitor [package=cap-pth-small]
  U1 = Voltage Regulator - 5V [package="TO220 [THT]"]
  Clock = Crystal [frequency="4 MHz" package=THT]
  UART_transceiver = IC, DIP package, 20 pins [chip_label=MAX233]
  C4 = Capacitor [package=cap-pth-large]
  UART = male pin header, 5 pins [form="♂ (male)"]
  CAN_controller = IC, DIP package, 18 pins [chip_label=MCP2515]
  C2 = Capacitor [package=cap-pth-large]
  CAN_transceiver = IC, DIP package, 8 pins [chip_label=MC2551]  # not connected
  Latch = IC, DIP package, 20 pins [chip_label=SN74ALS573C]
  C5 = Ceramic Capacitor [capacitance="100 nF" package="0603 [SMD, multilayer]"]
  IC1 = DIP - 20 pins [chip_label=ADC0844CCN package="DIP (Dual Inline) [THT]"]

nets:
  GND: Microcontroller.pin1, Microcontroller.pin20, RESET.Pin_3, RESET.Pin_4, LED.cathode, LED.anode, VCC1.-, C3.2, U1.GND, UART_transceiver.pin6, C4.2, CAN_controller.pin9, C2.2, Latch.pin1, Latch.pin10, C5.1, IC1.AGND, IC1.DGND
  N1: Microcontroller.pin3, Microcontroller.pin9, RESET.Pin_1, RESET.Pin_2
  Rx: Microcontroller.pin10, UART_transceiver.pin3
  Tx: Microcontroller.pin11, UART_transceiver.pin2
  !WR: Microcontroller.pin16, IC1.!RD, IC1.!WR
  N2: Microcontroller.pin18, Clock.pin_1
  N3: Microcontroller.pin19, Clock.pin_0
  addr4: Microcontroller.pin21
  addr3: Microcontroller.pin22
  addr2: Microcontroller.pin23
  addr1: Microcontroller.pin24
  JTAG4: Microcontroller.pin25
  JTAG3: Microcontroller.pin26
  JTAG2: Microcontroller.pin27
  JTAG1: Microcontroller.pin28
  LE: Microcontroller.pin30, Latch.pin11
  data7: Microcontroller.pin32, Latch.pin9, IC1.DB7
  data6: Microcontroller.pin33, Latch.pin8, IC1.DB6
  data5: Microcontroller.pin34, Latch.pin7, IC1.DB5
  data4: Microcontroller.pin35, Latch.pin6, IC1.DB4
  data3: Microcontroller.pin36, Latch.pin5, IC1.DB3
  data2: Microcontroller.pin37, Latch.pin4, IC1.DB2
  data1: Microcontroller.pin38, Latch.pin3, IC1.DB1
  data0: Microcontroller.pin39, Latch.pin2, IC1.DB0
  5V: Microcontroller.pin40, U1.output_voltage, UART_transceiver.pin7, C4.1, CAN_controller.pin18, C2.1, Latch.pin20, C5.0, IC1.VREF, IC1.VCC
  N4: VCC1.+, C3.1, U1.input_voltage
  N5: UART_transceiver.pin4, UART.pin3
  N6: UART_transceiver.pin5, UART.pin4
  N7: UART_transceiver.pin10, UART_transceiver.pin16
  N8: UART_transceiver.pin11, UART_transceiver.pin15
  N9: UART_transceiver.pin12, UART_transceiver.pin17

notes:
  TTK4255 - Byggern, This is the breadboard for Industrial Embedded., 1

custom parts:
  DIP - 20 pins: A DIP stand-in part for whatever IC you want. With 20 pins on a 300mil dual inline package (DIP) footprint.
